// Logisim project DflipflopFina222l.circ as structural Verilog: 1 circuit, main circuit main
module main (
  input  E,
  input  in_2,
  input  in_3,
  input  in_4,
  input  in_5,
  input  [3:0] in_6,
  input  [3:0] in_7,
  input  [3:0] in_8,
  input  [3:0] in_9,
  input  [3:0] in_10
);

  wire and_1_out, and_2_out, and_3_out, and_4_out, and_5_out, and_6_out, and_7_out, and_8_out, and_9_out,
       and_10_out, and_11_out, and_12_out, and_13_out, and_14_out, and_15_out, and_16_out, and_17_out,
       and_18_out, and_19_out, and_20_out, and_21_out, and_22_out, and_23_out, and_24_out, clock_1_out,
       d_ff_1_qn, d_ff_2_qn, d_ff_3_qn, d_ff_4_qn, multiplexer_1_out, multiplexer_2_out, multiplexer_3_out,
       multiplexer_4_out, multiplexer_5_out, multiplexer_6_out, multiplexer_7_out, multiplexer_8_out,
       not_1_out, or_1_out, or_2_out, or_3_out, or_4_out;
  wire [3:0] d_ff_4_q;

  not not_1 (not_1_out, E);
  Clock clock_1 (.out(clock_1_out));
  D_Flip_Flop d_ff_1 (
    .clk(clock_1_out), .D(or_1_out), .Q(d_ff_4_q[3]), .Qn(d_ff_1_qn), .reset(in_2));  // open: preset, en
  D_Flip_Flop d_ff_2 (
    .clk(clock_1_out), .D(or_4_out), .Q(d_ff_4_q[2]), .Qn(d_ff_2_qn), .reset(in_3));  // open: preset, en
  D_Flip_Flop d_ff_3 (
    .clk(clock_1_out), .D(or_2_out), .Q(d_ff_4_q[1]), .Qn(d_ff_3_qn), .reset(in_4));  // open: preset, en
  D_Flip_Flop d_ff_4 (
    .clk(clock_1_out), .D(or_3_out), .Q(d_ff_4_q[0]), .Qn(d_ff_4_qn), .reset(in_5));  // open: preset, en
  and and_1 (and_1_out, not_1_out, d_ff_4_q[3], d_ff_2_qn);
  and and_2 (and_2_out, not_1_out, d_ff_4_q[3], d_ff_3_qn);
  and and_3 (and_3_out, d_ff_4_q[3], d_ff_2_qn, d_ff_3_qn);
  and and_4 (and_4_out, d_ff_4_q[3], d_ff_2_qn, d_ff_4_qn);
  and and_5 (and_5_out, E, d_ff_1_qn, d_ff_4_q[2]);
  and and_6 (and_6_out, d_ff_4_q[2], d_ff_4_q[1], d_ff_4_q[0]);
  and and_7 (and_7_out, not_1_out, d_ff_4_q[2], d_ff_3_qn);
  and and_8 (and_8_out, E, d_ff_1_qn, d_ff_2_qn);
  and and_9 (and_9_out, E, d_ff_2_qn, d_ff_3_qn);
  and and_10 (and_10_out, not_1_out, d_ff_2_qn, d_ff_4_q[1], d_ff_4_q[0]);
  and and_11 (and_11_out, d_ff_1_qn, d_ff_4_q[2], d_ff_4_qn, not_1_out);
  and and_12 (and_12_out, not_1_out, d_ff_3_qn, d_ff_4_q[0]);
  and and_13 (and_13_out, d_ff_1_qn, d_ff_4_q[1], d_ff_4_qn);
  and and_14 (and_14_out, d_ff_2_qn, d_ff_4_q[1], d_ff_4_qn);
  and and_15 (and_15_out, E, d_ff_1_qn, d_ff_4_q[1]);
  and and_16 (and_16_out, E, d_ff_4_q[1], d_ff_4_qn);
  and and_17 (and_17_out, not_1_out, d_ff_1_qn, d_ff_4_qn);
  and and_18 (and_18_out, not_1_out, d_ff_2_qn, d_ff_4_qn);
  and and_19 (and_19_out, not_1_out, d_ff_3_qn, d_ff_4_qn);
  and and_20 (and_20_out, d_ff_2_qn, d_ff_4_q[1], d_ff_4_q[0], E);
  and and_21 (and_21_out, E, d_ff_1_qn, d_ff_4_q[0]);
  and and_22 (and_22_out, E, d_ff_4_q[3], d_ff_4_q[2], d_ff_4_qn);
  or or_1 (or_1_out, and_1_out, and_2_out, and_3_out, and_4_out, and_6_out, and_5_out);
  and and_23 (and_23_out, E, d_ff_2_qn, d_ff_4_qn);
  or or_2 (or_2_out, and_12_out, and_13_out, and_14_out, and_15_out, and_16_out, and_24_out);
  and and_24 (and_24_out, d_ff_4_q[3], d_ff_4_q[2], d_ff_4_q[0]);
  or or_3 (or_3_out, and_17_out, and_18_out, and_19_out, and_21_out, and_20_out, and_22_out);
  or or_4 (or_4_out, and_7_out, and_8_out, and_9_out, and_10_out, and_11_out, and_23_out);
  Multiplexer #(.select(4)) multiplexer_1 (
    .in0(1'b1), .in1(1'b1), .in2(1'b1), .in3(1'b1), .in4(1'b1), .in5(1'b1), .in6(1'b0), .in7(1'b0),
    .in8(1'b1), .in9(1'b1), .in10(1'b1), .in11(1'b1), .in12(1'b1), .in13(1'b0), .in14(1'b0), .in15(1'b1),
    .out(multiplexer_1_out), .sel(d_ff_4_q), .en(1'b1));
  Multiplexer #(.select(4)) multiplexer_2 (
    .in0(1'b1), .in1(1'b0), .in2(1'b0), .in3(1'b0), .in4(1'b1), .in5(1'b1), .in6(1'b1), .in7(1'b0),
    .in8(1'b1), .in9(1'b0), .in10(1'b1), .in11(1'b1), .in12(1'b1), .in13(1'b0), .in14(1'b0), .in15(1'b1),
    .out(multiplexer_2_out), .sel(d_ff_4_q), .en(1'b1));
  Multiplexer #(.select(4)) multiplexer_3 (
    .in0(1'b1), .in2(1'b1), .in5(1'b1), .in6(1'b1), .in8(1'b1), .in9(1'b1), .in10(1'b1), .in13(1'b1),
    .in14(1'b1), .in15(1'b1), .out(multiplexer_3_out), .sel(d_ff_4_q), .en(1'b1));  // open: in1, in3, in4, in7, in11, in12
  Multiplexer #(.select(4)) multiplexer_4 (
    .in0(1'b1), .in1(1'b1), .in2(1'b1), .in3(1'b1), .in4(1'b1), .in5(1'b1), .in9(1'b1), .in10(1'b1),
    .in11(1'b1), .in14(1'b1), .in15(1'b1), .out(multiplexer_4_out), .sel(d_ff_4_q), .en(1'b1));  // open: in6, in7, in8, in12, in13
  Multiplexer #(.select(4)) multiplexer_5 (
    .in0(1'b1), .in1(1'b1), .in3(1'b1), .in4(1'b1), .in9(1'b1), .in10(1'b1), .in11(1'b1), .in12(1'b1),
    .in13(1'b1), .in14(1'b1), .in15(1'b1), .out(multiplexer_5_out), .sel(d_ff_4_q), .en(1'b1));  // open: in2, in5, in6, in7, in8
  Multiplexer #(.select(4)) multiplexer_6 (
    .in1(1'b1), .in2(1'b1), .in3(1'b1), .in9(1'b1), .in10(1'b1), .in12(1'b1), .out(multiplexer_6_out),
    .sel(d_ff_4_q), .en(1'b1));  // open: in0, in4, in5, in6, in7, in8, in11, in13, in14, in15
  Multiplexer #(.select(4)) multiplexer_7 (
    .in2(1'b1), .in3(1'b1), .in4(1'b1), .in5(1'b1), .in11(1'b1), .in12(1'b1), .in13(1'b1), .in14(1'b1),
    .out(multiplexer_7_out), .sel(d_ff_4_q), .en(1'b1));  // open: in0, in1, in6, in7, in8, in9, in10, in15
  Multiplexer #(.select(4)) multiplexer_8 (
    .in7(1'b1), .out(multiplexer_8_out), .sel(d_ff_4_q), .en(1'b1));  // open: in0, in1, in2, in3, in4, in5, in6, in8, in9, in10, in11, in12, in13, in14, in15
  _7_Segment_Display u_7_segment_display_1 (
    .g(multiplexer_7_out), .f(multiplexer_6_out), .a(multiplexer_1_out), .b(multiplexer_2_out),
    .e(multiplexer_5_out), .d(multiplexer_4_out), .c(multiplexer_3_out), .dp(multiplexer_8_out));

  // Notes on the sheet:
  //   A
  //   B
  //   C
  //   Da
  //   Db
  //   Dc
  //   Dd
  //   a
  //   c
  //   d
  //   e
  //   b
  //   f
  //   dot
endmodule
