// Logisim project basic-combi-tfc.circ as structural Verilog: 1 circuit, main circuit main
module main (
  input  A,
  input  in_2,
  input  C,
  input  D
);

  wire and_1_out, and_2_out, and_3_out, and_4_out, and_5_out, and_6_out, and_7_out, and_8_out, and_9_out,
       and_10_out, and_11_out, and_12_out, and_13_out, and_14_out, and_15_out, and_16_out, and_17_out,
       and_18_out, and_19_out, and_20_out, and_21_out, and_22_out, and_23_out, and_24_out, and_25_out,
       and_26_out, and_27_out, and_28_out, not_1_out, not_2_out, not_3_out, not_4_out, or_1_out, or_2_out,
       or_3_out, or_4_out, or_5_out, or_6_out, or_7_out;

  not not_1 (not_1_out, A);
  not not_2 (not_2_out, in_2);
  not not_3 (not_3_out, C);
  not not_4 (not_4_out, D);
  and and_1 (and_1_out, not_1_out, in_2, not_3_out);
  and and_2 (and_2_out, not_1_out, in_2, not_4_out);
  and and_3 (and_3_out, A, not_2_out, C);
  and and_4 (and_4_out, not_2_out, not_4_out);
  and and_5 (and_5_out, C, not_4_out);
  and and_6 (and_6_out, in_2, not_3_out, D);
  and and_7 (and_7_out, A, not_2_out, not_3_out);
  and and_8 (and_8_out, not_1_out, not_2_out);
  and and_9 (and_9_out, not_1_out, not_3_out);
  and and_10 (and_10_out, not_2_out, D);
  and and_11 (and_11_out, A, C);
  and and_12 (and_12_out, not_3_out, not_1_out);
  and and_13 (and_13_out, not_3_out, not_4_out);
  and and_14 (and_14_out, A, C);
  and and_15 (and_15_out, A, in_2);
  and and_16 (and_16_out, not_1_out, not_3_out, not_4_out);
  and and_17 (and_17_out, not_1_out, not_2_out, D);
  and and_18 (and_18_out, not_2_out, not_3_out, D);
  and and_19 (and_19_out, not_2_out, C, not_4_out);
  and and_20 (and_20_out, A, in_2);
  and and_21 (and_21_out, not_3_out, not_4_out);
  and and_22 (and_22_out, in_2, not_3_out);
  and and_23 (and_23_out, A, in_2);
  and and_24 (and_24_out, not_1_out, not_2_out, C);
  and and_25 (and_25_out, not_2_out, C, D);
  and and_26 (and_26_out, in_2, C, D);
  and and_27 (and_27_out, not_2_out, D);
  or or_1 (or_1_out, not_2_out, and_12_out, and_13_out);
  or or_2 (or_2_out, and_13_out, and_1_out, and_2_out, and_3_out);
  and and_28 (and_28_out, and_20_out, and_21_out);
  or or_3 (or_3_out, and_22_out, and_23_out, and_24_out, and_25_out);
  or or_4 (or_4_out, and_17_out, and_18_out, and_19_out, and_28_out);
  or or_5 (or_5_out, and_27_out, and_14_out, and_15_out, and_16_out);
  or or_6 (or_6_out, and_4_out, and_5_out, and_7_out, and_6_out);
  or or_7 (or_7_out, and_8_out, and_9_out, and_10_out, and_11_out);
  _7_Segment_Display u_7_segment_display_1 (
    .g(or_3_out), .f(or_4_out), .a(or_1_out), .b(or_2_out), .e(or_5_out), .d(or_7_out), .c(or_6_out),
    .dp(and_26_out));

  // Notes on the sheet:
  //   B
  //   a
  //   e
  //   b
  //   a
endmodule
