// Logisim project Sec-8 G-08 BasicGates.circ as structural Verilog: 1 circuit, main circuit main
module main (
  input  P,
  input  Q,
  input  R,
  input  S
);

  wire a_out, and_1_out, and_2_out, and_3_out, and_4_out, and_5_out, and_6_out, and_7_out, and_8_out,
       and_9_out, and_10_out, and_11_out, and_12_out, and_13_out, and_14_out, and_15_out, and_16_out,
       and_17_out, and_18_out, and_19_out, and_20_out, and_21_out, and_22_out, and_23_out, and_24_out,
       and_25_out, b_out, c_out, d_out, dot_out, e_out, f_out, g_out, not_1_out, not_2_out, not_3_out,
       not_4_out;

  not not_1 (not_1_out, P);
  not not_2 (not_2_out, Q);
  not not_3 (not_3_out, R);
  not not_4 (not_4_out, S);
  and and_1 (and_1_out, not_1_out, not_3_out, not_4_out);
  and and_2 (and_2_out, R, S);
  and and_3 (and_3_out, R, P);
  and and_4 (and_4_out, Q, R, S);
  and and_5 (and_5_out, not_2_out, not_3_out);
  and and_6 (and_6_out, P, not_2_out);
  and and_7 (and_7_out, not_2_out, not_4_out);
  and and_8 (and_8_out, not_1_out, Q, not_3_out);
  and and_9 (and_9_out, P, not_2_out, S);
  and and_10 (and_10_out, P, R);
  and and_11 (and_11_out, R, S);
  and and_12 (and_12_out, not_1_out, not_2_out, S);
  and and_13 (and_13_out, Q, not_3_out, not_4_out);
  and and_14 (and_14_out, P, Q, not_3_out);
  and and_15 (and_15_out, not_2_out, R);
  and and_16 (and_16_out, R, S);
  and and_17 (and_17_out, P, not_4_out);
  and and_18 (and_18_out, Q, S);
  and and_19 (and_19_out, not_3_out, S);
  and and_20 (and_20_out, Q, not_3_out);
  and and_21 (and_21_out, not_1_out, R, S);
  and and_22 (and_22_out, P, not_3_out, S);
  and and_23 (and_23_out, P, R, not_4_out);
  and and_24 (and_24_out, not_1_out, not_2_out);
  and and_25 (and_25_out, not_2_out, not_3_out);
  or a (a_out, and_1_out, and_2_out, and_3_out, not_2_out);
  or f (f_out, and_4_out, and_5_out, and_6_out, and_7_out);
  or b (b_out, and_8_out, and_9_out, and_10_out, and_11_out);
  or g (g_out, and_12_out, and_13_out, and_14_out, and_15_out, and_16_out);
  or e (e_out, and_16_out, and_7_out, P);
  or c (c_out, and_17_out, and_18_out, and_19_out, and_20_out);
  or d (d_out, and_1_out, and_21_out, and_22_out, and_23_out, and_24_out, and_25_out);
  and dot (dot_out, not_1_out, Q, R, not_4_out);
  _7_Segment_Display u_7_segment_display_1 (
    .g(g_out), .f(f_out), .a(a_out), .b(b_out), .e(e_out), .d(d_out), .c(c_out), .dp(dot_out));
endmodule
