// Logisim project Sec-8 G-08 J-K-Flip-Flop.circ as structural Verilog: 3 circuits, main circuit main
module main (
  input  Control_To_Skip_3,
  input  Clear
);

  wire CLK_out, j_k_flip_flops_1_p, j_k_flip_flops_1_q, j_k_flip_flops_1_r, j_k_flip_flops_1_s,
       universalgatescombi_1_a, universalgatescombi_1_b, universalgatescombi_1_c, universalgatescombi_1_d,
       universalgatescombi_1_dot, universalgatescombi_1_e, universalgatescombi_1_f, universalgatescombi_1_g;

  Clock CLK (.out(CLK_out));
  J_k_Flip_Flops j_k_flip_flops_1 (
    .Reset(Clear), .I(Control_To_Skip_3), .P(j_k_flip_flops_1_p), .Q(j_k_flip_flops_1_q),
    .R(j_k_flip_flops_1_r), .S(j_k_flip_flops_1_s), .Clk(CLK_out));
  UniversalGatesCombi universalgatescombi_1 (
    .P(j_k_flip_flops_1_p), .Q(j_k_flip_flops_1_q), .R(j_k_flip_flops_1_r), .S(j_k_flip_flops_1_s),
    .a(universalgatescombi_1_a), .f(universalgatescombi_1_f), .b(universalgatescombi_1_b),
    .g(universalgatescombi_1_g), .e(universalgatescombi_1_e), .c(universalgatescombi_1_c),
    .d(universalgatescombi_1_d), .dot(universalgatescombi_1_dot));
  _7_Segment_Display u_7_segment_display_1 (
    .g(universalgatescombi_1_g), .f(universalgatescombi_1_f), .a(universalgatescombi_1_a),
    .b(universalgatescombi_1_b), .e(universalgatescombi_1_e), .d(universalgatescombi_1_d),
    .c(universalgatescombi_1_c), .dp(universalgatescombi_1_dot));
endmodule

// J-K FFs
module J_k_Flip_Flops (
  input  Reset,
  input  I,
  input  Clk,
  output P,
  output Q,
  output R,
  output S
);

  wire and_1_out, and_2_out, and_3_out, and_4_out, and_5_out, and_6_out, and_7_out, and_8_out, and_9_out,
       and_10_out, and_11_out, and_12_out, and_13_out, and_14_out, and_15_out, and_16_out, and_17_out,
       and_18_out, and_19_out, and_20_out, and_21_out, and_22_out, JP_out, JQ_out, JR_out, JS_out, KP_out,
       KQ_out, KR_out, KS_out, not_1_out, P_qn, Q_qn, R_qn, S_qn, undriven, undriven_2, undriven_3;

  not not_1 (not_1_out, I);
  J_K_Flip_Flop u_P (
    .J(JP_out), .clk(Clk), .K(KP_out), .Q(P), .Qn(P_qn), .en(undriven), .reset(Reset));  // open: preset
  J_K_Flip_Flop u_Q (
    .J(JQ_out), .clk(Clk), .K(KQ_out), .Q(Q), .Qn(Q_qn), .en(undriven_2), .reset(Reset));  // open: preset
  J_K_Flip_Flop u_R (
    .J(JR_out), .clk(Clk), .K(KR_out), .Q(R), .Qn(R_qn), .en(undriven_3), .reset(Reset));  // open: preset
  J_K_Flip_Flop u_S (.J(JS_out), .clk(Clk), .K(KS_out), .Q(S), .Qn(S_qn), .reset(Reset));  // open: preset, en
  and and_1 (and_1_out, Q, R, S);
  and and_2 (and_2_out, Q, R);
  and and_3 (and_3_out, I, Q);
  or JP (JP_out, and_1_out, and_3_out);
  and and_4 (and_4_out, I, Q);
  and and_5 (and_5_out, I, R, S);
  or KP (KP_out, and_2_out, and_4_out, and_5_out);
  and and_6 (and_6_out, I, R_qn);
  and and_7 (and_7_out, I, P_qn);
  and and_8 (and_8_out, not_1_out, R, S);
  or JQ (JQ_out, and_8_out, and_7_out, and_6_out, and_10_out);
  and and_9 (and_9_out, R, S);
  and and_10 (and_10_out, I, S_qn);
  and and_11 (and_11_out, P, R);
  or KQ (KQ_out, and_9_out, and_11_out, I);
  and and_12 (and_12_out, not_1_out, S);
  and and_13 (and_13_out, P, Q, S);
  or JR (JR_out, and_12_out, and_13_out);
  and and_14 (and_14_out, not_1_out, S);
  and and_15 (and_15_out, P, S);
  and and_16 (and_16_out, not_1_out, P, Q);
  or KR (KR_out, and_14_out, and_15_out, and_16_out);
  and and_17 (and_17_out, not_1_out, P_qn);
  and and_18 (and_18_out, not_1_out, Q_qn);
  and and_19 (and_19_out, I, P, Q);
  and and_20 (and_20_out, not_1_out, R_qn);
  or JS (JS_out, and_17_out, and_18_out, and_20_out, and_19_out);
  and and_21 (and_21_out, P, Q);
  and and_22 (and_22_out, P, R);
  or KS (KS_out, not_1_out, and_22_out, and_21_out);
endmodule

// NANDs
module UniversalGatesCombi (
  input  P,
  input  Q,
  input  R,
  input  S,
  output a,
  output f,
  output b,
  output g,
  output e,
  output c,
  output d,
  output dot
);

  wire nand_1_out, nand_2_out, nand_3_out, nand_4_out, nand_5_out, nand_6_out, nand_7_out, nand_8_out,
       nand_9_out, nand_10_out, nand_11_out, nand_12_out, nand_13_out, nand_14_out, nand_15_out, nand_16_out,
       nand_17_out, nand_18_out, nand_19_out, nand_20_out, nand_21_out, nand_22_out, nand_23_out,
       nand_24_out, nand_25_out, nand_26_out, nand_27_out, nand_28_out, nand_29_out, nand_30_out,
       nand_31_out, nand_32_out, nand_33_out;

  nand nand_1 (nand_1_out, P, P);
  nand nand_2 (nand_2_out, Q, Q);
  nand nand_3 (nand_3_out, R, R);
  nand nand_4 (nand_4_out, S, S);
  nand nand_5 (nand_5_out, nand_1_out, nand_3_out, nand_4_out);
  nand nand_6 (nand_6_out, R, S);
  nand nand_7 (nand_7_out, P, R);
  nand nand_8 (nand_8_out, nand_2_out, nand_3_out);
  nand nand_9 (nand_9_out, nand_2_out, nand_4_out);
  nand nand_10 (nand_10_out, Q, R, S);
  nand nand_11 (nand_11_out, P, nand_2_out);
  nand nand_12 (nand_12_out, R, S);
  nand nand_13 (nand_13_out, nand_1_out, Q, nand_3_out);
  nand nand_14 (nand_14_out, P, nand_2_out, S);
  nand nand_15 (nand_15_out, P, R);
  nand nand_16 (nand_16_out, nand_1_out, nand_2_out, S);
  nand nand_17 (nand_17_out, nand_2_out, R);
  nand nand_18 (nand_18_out, R, S);
  nand nand_19 (nand_19_out, Q, nand_3_out, nand_4_out);
  nand nand_20 (nand_20_out, P, Q, nand_3_out);
  nand nand_21 (nand_21_out, nand_2_out, nand_4_out);
  nand nand_22 (nand_22_out, R, S);
  nand nand_23 (nand_23_out, nand_3_out, S);
  nand nand_24 (nand_24_out, Q, nand_3_out);
  nand nand_25 (nand_25_out, Q, S);
  nand nand_26 (nand_26_out, P, nand_4_out);
  nand nand_27 (nand_27_out, nand_1_out, nand_2_out);
  nand nand_28 (nand_28_out, nand_1_out, nand_3_out, nand_4_out);
  nand nand_29 (nand_29_out, nand_2_out, nand_3_out);
  nand nand_30 (nand_30_out, nand_1_out, R, S);
  nand nand_31 (nand_31_out, P, nand_3_out, S);
  nand nand_32 (nand_32_out, P, R, nand_4_out);
  nand nand_33 (nand_33_out, nand_1_out, Q, R, nand_4_out);
  nand nand_34 (e, nand_21_out, nand_22_out, nand_1_out);
  nand nand_35 (dot, nand_33_out, nand_33_out);
  nand nand_36 (a, nand_5_out, Q, nand_6_out, nand_7_out);
  nand nand_37 (f, nand_8_out, nand_9_out, nand_10_out, nand_11_out);
  nand nand_38 (b, nand_12_out, nand_13_out, nand_14_out, nand_15_out);
  nand nand_39 (g, nand_16_out, nand_17_out, nand_18_out, nand_19_out, nand_20_out);
  nand nand_40 (c, nand_23_out, nand_24_out, nand_25_out, nand_26_out);
  nand nand_41 (d, nand_27_out, nand_28_out, nand_29_out, nand_30_out, nand_31_out, nand_32_out);
endmodule
