// Logisim project Sec-8-G-08-J-K-Flip-Flop.circ as structural Verilog: 2 circuits, main circuit main
module main (
  input  Control_To_Skip_3,
  input  Reset
);

  wire CLK_out, j_k_flip_flops_1_p, j_k_flip_flops_1_q, j_k_flip_flops_1_r, j_k_flip_flops_1_s,
       universalimp_1_a, universalimp_1_b, universalimp_1_c, universalimp_1_d, universalimp_1_dot,
       universalimp_1_e, universalimp_1_f, universalimp_1_g;

  Clock CLK (.out(CLK_out));
  J_k_Flip_Flops j_k_flip_flops_1 (
    .Reset(Reset), .I(Control_To_Skip_3), .P(j_k_flip_flops_1_p), .Q(j_k_flip_flops_1_q),
    .R(j_k_flip_flops_1_r), .S(j_k_flip_flops_1_s), .Clk(CLK_out));
  UniversalImp universalimp_1 (
    .a(universalimp_1_a), .f(universalimp_1_f), .b(universalimp_1_b), .g(universalimp_1_g),
    .e(universalimp_1_e), .c(universalimp_1_c), .d(universalimp_1_d), .dot(universalimp_1_dot),
    .P(j_k_flip_flops_1_p), .Q(j_k_flip_flops_1_q), .R(j_k_flip_flops_1_r), .S(j_k_flip_flops_1_s));
  _7_Segment_Display u_7_segment_display_1 (
    .g(universalimp_1_g), .f(universalimp_1_f), .a(universalimp_1_a), .b(universalimp_1_b),
    .e(universalimp_1_e), .d(universalimp_1_d), .c(universalimp_1_c), .dp(universalimp_1_dot));
endmodule

// J-K FFs
module J_k_Flip_Flops (
  input  Reset,
  input  I,
  input  Clk,
  output P,
  output Q,
  output R,
  output S
);

  wire and_1_out, and_2_out, and_3_out, and_4_out, and_5_out, and_6_out, and_7_out, and_8_out, and_9_out,
       and_10_out, and_11_out, and_12_out, and_13_out, and_14_out, and_15_out, and_16_out, and_17_out,
       and_18_out, and_19_out, and_20_out, and_21_out, and_22_out, not_1_out, or_1_out, or_2_out, or_3_out,
       or_4_out, or_5_out, or_6_out, or_7_out, or_8_out, P_qn, Q_qn, R_qn, S_qn, undriven, undriven_2,
       undriven_3;

  not not_1 (not_1_out, I);
  J_K_Flip_Flop u_P (
    .J(or_1_out), .clk(Clk), .K(or_2_out), .Q(P), .Qn(P_qn), .en(undriven), .reset(Reset));  // open: preset
  J_K_Flip_Flop u_Q (
    .J(or_3_out), .clk(Clk), .K(or_4_out), .Q(Q), .Qn(Q_qn), .en(undriven_2), .reset(Reset));  // open: preset
  J_K_Flip_Flop u_R (
    .J(or_5_out), .clk(Clk), .K(or_6_out), .Q(R), .Qn(R_qn), .en(undriven_3), .reset(Reset));  // open: preset
  J_K_Flip_Flop u_S (.J(or_7_out), .clk(Clk), .K(or_8_out), .Q(S), .Qn(S_qn), .reset(Reset));  // open: preset, en
  and and_1 (and_1_out, Q, R, S);
  and and_2 (and_2_out, I, Q);
  and and_3 (and_3_out, Q, R);
  or or_1 (or_1_out, and_1_out, and_2_out);
  and and_4 (and_4_out, I, Q);
  and and_5 (and_5_out, I, R, S);
  or or_2 (or_2_out, and_3_out, and_4_out, and_5_out);
  and and_6 (and_6_out, I, P_qn);
  and and_7 (and_7_out, I, R_qn);
  and and_8 (and_8_out, not_1_out, R, S);
  or or_3 (or_3_out, and_8_out, and_6_out, and_7_out, and_10_out);
  and and_9 (and_9_out, R, S);
  and and_10 (and_10_out, I, S_qn);
  and and_11 (and_11_out, P, R);
  or or_4 (or_4_out, and_9_out, and_11_out, I);
  and and_12 (and_12_out, not_1_out, S);
  and and_13 (and_13_out, P, Q, S);
  or or_5 (or_5_out, and_12_out, and_13_out);
  and and_14 (and_14_out, not_1_out, S);
  and and_15 (and_15_out, P, S);
  and and_16 (and_16_out, not_1_out, P, Q);
  or or_6 (or_6_out, and_14_out, and_15_out, and_16_out);
  and and_17 (and_17_out, not_1_out, P_qn);
  and and_18 (and_18_out, not_1_out, Q_qn);
  and and_19 (and_19_out, not_1_out, R_qn);
  and and_20 (and_20_out, I, P, Q);
  or or_7 (or_7_out, and_17_out, and_18_out, and_19_out, and_20_out);
  and and_21 (and_21_out, P, R);
  and and_22 (and_22_out, P, Q);
  or or_8 (or_8_out, not_1_out, and_21_out, and_22_out);
endmodule
