// Logisim project First.circ as structural Verilog: 4 circuits, main circuit main
module main (
  input  A,
  input  B,
  input  C,
  output out_4
);

  wire n7404_1_out_11, n7404_1_out_12, n7408_1_out_9, n7408_1_out_11, n7408_1_out_12, n74732_1_out_10;

  _7404 u_7404_1 (
    .in_5(B), .in_6(A), .out_11(n7404_1_out_11), .out_12(n7404_1_out_12));  // open: in_1, in_2, in_3, in_4, out_7, out_8, out_9, out_10
  _7408 u_7408_1 (
    .in_1(C), .in_2(B), .in_5(n7404_1_out_11), .in_6(A), .in_7(C), .in_8(n7404_1_out_12),
    .out_9(n7408_1_out_9), .out_11(n7408_1_out_11), .out_12(n7408_1_out_12));  // open: in_3, in_4, out_10
  _74732 u_74732_1 (
    .in_1(n7408_1_out_9), .in_2(n74732_1_out_10), .in_3(n7408_1_out_11), .in_4(n7408_1_out_12),
    .out_9(out_4), .out_10(n74732_1_out_10));  // open: in_5, in_6, in_7, in_8, out_11, out_12

  // Notes on the sheet:
  //   B
  //   B'
  //   A'
  //   C
  //   B'
  //   A
  //   BC
  //   AB'
  //   A'C
  //   F = A'C + AB' + BC 
endmodule

module _7408 (
  input  in_1,
  input  in_2,
  input  in_3,
  input  in_4,
  input  in_5,
  input  in_6,
  input  in_7,
  input  in_8,
  output out_9,
  output out_10,
  output out_11,
  output out_12
);

  and and_1 (out_9, in_1, in_2);
  and and_2 (out_10, in_3, in_4);
  and and_3 (out_11, in_5, in_6);
  and and_4 (out_12, in_7, in_8);
endmodule

module _7404 (
  input  in_1,
  input  in_2,
  input  in_3,
  input  in_4,
  input  in_5,
  input  in_6,
  output out_7,
  output out_8,
  output out_9,
  output out_10,
  output out_11,
  output out_12
);

  not not_1 (out_7, in_1);
  not not_2 (out_8, in_2);
  not not_3 (out_9, in_3);
  not not_4 (out_10, in_4);
  not not_5 (out_11, in_5);
  not not_6 (out_12, in_6);
endmodule

module _74732 (
  input  in_1,
  input  in_2,
  input  in_3,
  input  in_4,
  input  in_5,
  input  in_6,
  input  in_7,
  input  in_8,
  output out_9,
  output out_10,
  output out_11,
  output out_12
);

  or or_1 (out_9, in_1, in_2);
  or or_2 (out_10, in_3, in_4);
  or or_3 (out_11, in_5, in_6);
  or or_4 (out_12, in_7, in_8);
endmodule
