// Logisim project Week 2 task 2.circ as structural Verilog: 1 circuit, main circuit main
module main (
  input  A,
  input  B,
  input  A_2,
  input  A_3,
  input  in_5,
  input  A_4,
  input  B_2,
  input  A_5,
  input  A_6,
  input  B_3,
  input  B_4,
  input  in_12,
  input  in_13,
  output out_14,
  output A_prime,
  output out_16,
  output AB,
  output A_B,
  output AB___A_prime_B_prime,
  output AB____A_prime_B_prime
);

  wire nand_1_out, nand_2_out, nand_3_out, nand_4_out, nand_5_out, nand_6_out, nand_7_out, nor_1_out,
       nor_2_out, nor_3_out, nor_4_out, nor_5_out, nor_6_out, nor_7_out, nor_11_out, nor_12_out, nor_13_out;

  nand nand_1 (nand_1_out, A, B);
  nor nor_1 (nor_1_out, A_3, A_3);
  nor nor_2 (nor_2_out, in_5, in_5);
  nor nor_3 (nor_3_out, A_3, in_5);
  nand nand_2 (nand_2_out, A_5, B_4);
  nor nor_4 (nor_4_out, in_12, in_13);
  nor nor_5 (nor_5_out, nor_1_out, nor_2_out);
  nand nand_3 (nand_3_out, A_5, nand_2_out);
  nand nand_4 (nand_4_out, nand_2_out, B_4);
  nor nor_6 (nor_6_out, in_12, nor_4_out);
  nor nor_7 (nor_7_out, nor_4_out, in_13);
  nand nand_5 (nand_5_out, A, nand_1_out);
  nand nand_6 (nand_6_out, nand_1_out, B);
  nor nor_8 (out_16, nor_5_out, nor_3_out);
  nand nand_7 (nand_7_out, nand_3_out, nand_4_out);
  nor nor_9 (AB____A_prime_B_prime, nor_6_out, nor_7_out);
  nand nand_8 (out_14, nand_5_out, nand_6_out);
  nand nand_9 (AB___A_prime_B_prime, nand_7_out, nand_7_out);
  nor nor_10 (A_prime, A_2, A_2);
  nor nor_11 (nor_11_out, A_4, A_4);
  nor nor_12 (nor_12_out, B_2, B_2);
  nor nor_13 (nor_13_out, A_6, B_3);
  nor nor_14 (AB, nor_11_out, nor_12_out);
  nor nor_15 (A_B, nor_13_out, nor_13_out);

  // Notes on the sheet:
  //   B
  //   A
  //   B
  //   Implementing XOR using NAND
  //   A'
  //   B'
  //   Implementing XOR gate using NOR gate
  //   (AB)'
  //   Implementing XNOR gate using NAND gate
  //   (A+B)'
  //   Implementing XNOR gate using NOR gate
  //   (AB)'
  //   (A + B)'
  //   (A' + B' )' = AB
  //   (A.(A.B)'  )'
  //   (B + (AB) ' )' = B' + AB
  //   (A (AB) ' )'
  //   (B (AB)' ) '
  //   (A + (A+B) ' )'
  //   (B + (A+B) ' )'
  //   = A' + (AB)
  //   (AB + (A + B)' )' = A'B + AB'
  //   ((A' + AB)(B' + AB))'
  //   Implementing NOT gate using NOR gate
  //   Implementing AND gate using NOR gate
  //   Implementing OR gate using NOR gate
  //   (A+A)'
  //   (B+B)'
  //   (A+B)'
  //   (A+B)'
endmodule
