// Logisim project Experiment 2.circ as structural Verilog: 1 circuit, main circuit main
module main (
  input  in_1,
  input  [2:0] A_B_C,
  input  D,
  output out_4
);

  Multiplexer #(.select(3)) multiplexer_1 (
    .in0(1'b1), .in1(D), .in2(D), .in3(in_1), .in4(1'b1), .in5(in_1), .in6(in_1), .in7(1'b1), .out(out_4),
    .sel(A_B_C));  // open: en

  // Notes on the sheet:
  //   F(A, B, C, D) = Σ (0, 1, 3, 5, 8, 9, 14, 15)
endmodule
