// Logisim project Sequential Circuit Using D-Flipflop.circ as structural Verilog: 1 circuit, main circuit main
module main (
  input  X,
  output out_2,
  output DB___B_prime
);

  wire clock_1_out, d_ff_2_qn, xor_1_out;

  ExactlyOne xor_1 (.out(xor_1_out), .in0(out_2), .in1(X), .in2(DB___B_prime));
  Clock clock_1 (.out(clock_1_out));
  D_Flip_Flop d_ff_1 (.clk(clock_1_out), .D(xor_1_out), .Q(out_2));  // open: Qn, preset, en, reset
  D_Flip_Flop d_ff_2 (.clk(clock_1_out), .D(d_ff_2_qn), .Q(DB___B_prime), .Qn(d_ff_2_qn));  // open: preset, en, reset

  // Notes on the sheet:
  //   B
  //   A
  //   Sequential Circuit Using D-Flipflop
  //   DA
  //   DB
  //   DA = (A xor B) xor X
endmodule
