// Logisim project Design the circuit using Multiplexer.circ as structural Verilog: 1 circuit, main circuit main
module main (
  input  [2:0] X_Y_Z
);

  wire multiplexer_1_out, multiplexer_2_out, multiplexer_3_out, multiplexer_4_out, multiplexer_5_out,
       multiplexer_6_out;

  Multiplexer #(.select(3)) multiplexer_1 (
    .in0(1'b0), .in1(1'b1), .in2(1'b1), .in3(1'b1), .in4(1'b1), .in5(1'b1), .in6(1'b1), .in7(1'b0),
    .out(multiplexer_1_out), .sel(X_Y_Z));  // open: en
  Multiplexer #(.select(3)) multiplexer_2 (
    .in0(1'b1), .in1(1'b1), .in2(1'b1), .in3(1'b1), .in4(1'b1), .in5(1'b0), .in6(1'b1), .in7(1'b0),
    .out(multiplexer_2_out), .sel(X_Y_Z));  // open: en
  Multiplexer #(.select(3)) multiplexer_3 (
    .in0(1'b1), .in1(1'b1), .in2(1'b0), .in3(1'b0), .in4(1'b1), .in5(1'b1), .in6(1'b1), .in7(1'b0),
    .out(multiplexer_3_out), .sel(X_Y_Z));  // open: en
  Multiplexer #(.select(3)) multiplexer_4 (
    .in0(1'b0), .in1(1'b0), .in2(1'b1), .in3(1'b1), .in4(1'b1), .in5(1'b0), .in6(1'b1), .in7(1'b0),
    .out(multiplexer_4_out), .sel(X_Y_Z));  // open: en
  Multiplexer #(.select(3)) multiplexer_5 (
    .in0(1'b0), .in1(1'b1), .in2(1'b0), .in3(1'b0), .in4(1'b1), .in5(1'b1), .in6(1'b1), .in7(1'b0),
    .out(multiplexer_5_out), .sel(X_Y_Z));  // open: en
  Multiplexer #(.select(3)) multiplexer_6 (
    .in0(1'b0), .in1(1'b1), .in2(1'b1), .in3(1'b1), .in4(1'b0), .in5(1'b1), .in6(1'b0), .in7(1'b0),
    .out(multiplexer_6_out), .sel(X_Y_Z));  // open: en
  _7_Segment_Display u_7_segment_display_1 (
    .g(multiplexer_6_out), .f(multiplexer_5_out), .a(multiplexer_1_out), .b(multiplexer_2_out),
    .e(multiplexer_4_out), .d(multiplexer_1_out), .c(multiplexer_3_out));  // open: dp

  // Notes on the sheet:
  //   a = (1,2,3,4,5,6)
  //   b = (0,1,2,3,4,6)
  //   c = (0,1,4,5,6)
  //   e = (2,3,4,6)
  //   f = (1,4,5,6)
  //   g = (1,2,3,5)
  //   d = (1,2,3,4,5,6)
endmodule
