// Logisim project Design the circuit using NOR gates only.circ as structural Verilog: 1 circuit, main circuit main
module main (
  input  X,
  input  Y,
  input  Z
);

  wire nor_1_out, nor_2_out, nor_3_out, nor_4_out, nor_5_out, nor_6_out, nor_7_out, nor_8_out, nor_9_out,
       nor_10_out, nor_11_out, nor_12_out, nor_13_out, nor_14_out, nor_15_out, nor_16_out, nor_17_out,
       nor_18_out, nor_19_out, nor_20_out, nor_21_out;

  nor nor_1 (nor_1_out, X, Y, Z);
  nor nor_2 (nor_2_out, X, X);
  nor nor_3 (nor_3_out, Z, Z);
  nor nor_4 (nor_4_out, Y, Y);
  nor nor_5 (nor_5_out, X, X);
  nor nor_6 (nor_6_out, Z, Z);
  nor nor_7 (nor_7_out, Y, Y);
  nor nor_8 (nor_8_out, Y, nor_6_out);
  nor nor_9 (nor_9_out, X, nor_7_out);
  nor nor_10 (nor_10_out, nor_1_out, nor_1_out);
  nor nor_11 (nor_11_out, nor_2_out, nor_3_out);
  nor nor_12 (nor_12_out, X, nor_4_out);
  nor nor_13 (nor_13_out, nor_5_out, Z);
  nor nor_14 (nor_14_out, nor_11_out, nor_11_out);
  nor nor_15 (nor_15_out, nor_12_out, nor_12_out);
  nor nor_16 (nor_16_out, nor_13_out, Y);
  nor nor_17 (nor_17_out, nor_8_out, X);
  nor nor_18 (nor_18_out, nor_9_out, Z);
  nor nor_19 (nor_19_out, nor_16_out, nor_16_out);
  nor nor_20 (nor_20_out, nor_17_out, nor_17_out);
  nor nor_21 (nor_21_out, nor_18_out, nor_18_out);
  _7_Segment_Display u_7_segment_display_1 (
    .g(nor_21_out), .f(nor_20_out), .a(nor_10_out), .b(nor_14_out), .e(nor_19_out), .d(nor_10_out),
    .c(nor_15_out));  // open: dp

  // Notes on the sheet:
  //   a = X + Y + Z
  //   b = X' + Z'
  //   c = X + Y'
  //   e = Y + XZ'
endmodule
