// Logisim project Generalized SOP circuit with basic gates.circ as structural Verilog: 1 circuit, main circuit main
module main (
  input  X,
  input  Y,
  input  Z
);

  wire and_1_out, and_2_out, and_3_out, and_4_out, and_5_out, and_6_out, and_7_out, and_8_out, and_9_out,
       and_10_out, and_11_out, and_12_out, and_13_out, and_14_out, and_15_out, and_16_out, and_17_out,
       and_18_out, and_19_out, and_20_out, and_21_out, and_22_out, and_23_out, and_24_out, and_25_out,
       and_26_out, and_27_out, and_28_out, and_29_out, not_1_out, not_2_out, not_3_out, or_1_out, or_2_out,
       or_3_out, or_4_out, or_5_out, or_6_out, or_7_out, or_8_out, or_9_out, or_10_out, or_11_out, or_12_out,
       or_13_out, or_14_out, or_15_out;

  not not_1 (not_1_out, X);
  not not_2 (not_2_out, Y);
  not not_3 (not_3_out, Z);
  and and_1 (and_1_out, X, Y, not_3_out);
  and and_2 (and_2_out, X, not_2_out, Z);
  and and_3 (and_3_out, X, not_2_out, not_3_out);
  and and_4 (and_4_out, not_1_out, Y, Z);
  and and_5 (and_5_out, not_1_out, Y, not_3_out);
  and and_6 (and_6_out, not_1_out, not_2_out, Z);
  and and_7 (and_7_out, not_1_out, Y, Z);
  and and_8 (and_8_out, not_1_out, Y, not_3_out);
  and and_9 (and_9_out, not_1_out, not_2_out, Z);
  and and_10 (and_10_out, not_1_out, not_2_out, not_3_out);
  and and_11 (and_11_out, X, Y, not_3_out);
  and and_12 (and_12_out, X, not_2_out, not_3_out);
  and and_13 (and_13_out, X, not_2_out, Z);
  and and_14 (and_14_out, X, not_2_out, not_3_out);
  and and_15 (and_15_out, not_1_out, not_2_out, Z);
  and and_16 (and_16_out, not_1_out, not_2_out, not_3_out);
  and and_17 (and_17_out, X, Y, not_3_out);
  and and_18 (and_18_out, X, Y, not_3_out);
  and and_19 (and_19_out, not_1_out, Y, Z);
  and and_20 (and_20_out, not_1_out, Y, not_3_out);
  and and_21 (and_21_out, X, not_2_out, not_3_out);
  and and_22 (and_22_out, X, Y, not_3_out);
  and and_23 (and_23_out, X, not_2_out, Z);
  and and_24 (and_24_out, X, not_2_out, not_3_out);
  and and_25 (and_25_out, not_1_out, not_2_out, Z);
  and and_26 (and_26_out, X, not_2_out, Z);
  and and_27 (and_27_out, not_1_out, Y, Z);
  and and_28 (and_28_out, not_1_out, not_2_out, Z);
  and and_29 (and_29_out, not_1_out, Y, not_3_out);
  or or_1 (or_1_out, and_1_out, and_2_out);
  or or_2 (or_2_out, and_4_out, and_5_out, and_6_out);
  or or_3 (or_3_out, and_7_out, and_8_out, and_9_out);
  or or_4 (or_4_out, and_10_out, and_11_out, and_12_out);
  or or_5 (or_5_out, and_13_out, and_14_out, and_15_out);
  or or_6 (or_6_out, and_16_out, and_17_out);
  or or_7 (or_7_out, and_18_out, and_19_out, and_20_out);
  or or_8 (or_8_out, and_22_out, and_23_out);
  or or_9 (or_9_out, and_26_out, and_27_out);
  or or_10 (or_10_out, or_1_out, and_3_out, or_2_out);
  or or_11 (or_11_out, or_3_out, or_4_out);
  or or_12 (or_12_out, or_5_out, or_6_out);
  or or_13 (or_13_out, or_8_out, and_25_out, and_24_out);
  or or_14 (or_14_out, or_9_out, and_29_out, and_28_out);
  or or_15 (or_15_out, or_7_out, and_21_out);
  _7_Segment_Display u_7_segment_display_1 (
    .g(or_14_out), .f(or_13_out), .a(or_10_out), .b(or_11_out), .e(or_15_out), .d(or_10_out), .c(or_12_out));  // open: dp
endmodule
