// Logisim project Simplified POS circuit with basic gates.circ as structural Verilog: 1 circuit, main circuit main
module main (
  input  X,
  input  Y,
  input  Z
);

  wire and_1_out, and_2_out, and_3_out, not_1_out, not_2_out, not_3_out, not_4_out, not_5_out, not_6_out,
       or_1_out, or_2_out, or_3_out, or_4_out, or_5_out, or_6_out, or_7_out, or_8_out, or_9_out;

  not not_1 (not_1_out, X);
  not not_2 (not_2_out, Z);
  not not_3 (not_3_out, Y);
  not not_4 (not_4_out, Z);
  not not_5 (not_5_out, Y);
  not not_6 (not_6_out, X);
  or or_1 (or_1_out, X, Y, Z);
  or or_2 (or_2_out, not_1_out, not_2_out);
  or or_3 (or_3_out, X, not_3_out);
  or or_4 (or_4_out, X, Y);
  or or_5 (or_5_out, Y, not_4_out);
  or or_6 (or_6_out, X, Z);
  or or_7 (or_7_out, X, not_5_out);
  or or_8 (or_8_out, Y, Z);
  or or_9 (or_9_out, not_6_out, Z);
  and and_1 (and_1_out, or_4_out, or_5_out);
  and and_2 (and_2_out, or_6_out, or_7_out);
  and and_3 (and_3_out, or_8_out, or_9_out);
  _7_Segment_Display u_7_segment_display_1 (
    .g(and_3_out), .f(and_2_out), .a(or_1_out), .b(or_2_out), .e(and_1_out), .d(or_1_out), .c(or_3_out));  // open: dp
endmodule
